# Fritzing sketch ShutterGlasses (saved by Fritzing 0.6.3b)
breadboards: 2

parts:
  U1 = LM 358 Dual Op-Amp [package="DIP8 [THT]"]
  U2 = LM 358 Dual Op-Amp [package="DIP8 [THT]"]
  R1 = Resistor [resistance=15k tolerance=±5% package=THT]
  R2 = Resistor [resistance=15k tolerance=±5% package=THT]
  IC1 = IC, DIP package, 8 pins [chip_label=LT1301 spacing=300mil]
  L1 = Inductor [inductance=33µ package="400 mil [THT]"]
  D1 = Schottky Diode [part_number=1N5817 package="300 mil [THT]"]
  C1 = Ceramic Capacitor [capacitance=100nF package="200 mil [THT, multilayer]"]
  C2 = Electrolytic Capacitor [capacitance=47µF voltage=20V package="100 mil [THT, electrolytic]"]
  C3 = Electrolytic Capacitor [capacitance=47µF voltage=20V package="100 mil [THT, electrolytic]"]
  TRS1 = Stereo Jack (TRS) 3.5mm [package="PG203J [THT]"]
  IC2 = IC, DIP package, 8 pins [chip_label=AtTiny45 spacing=300mil]
  CONN1 = USB connector [package=THT]
  R3 = Resistor [tolerance=±5% resistance=150k package=THT]
  R4 = Resistor [tolerance=±5% resistance=150k package=THT]
  J1 = female pin header, 2 pins [form="♀ (female)"]
  XTAL1 = Crystal [frequency=8MHz package=THT]
  C4 = Ceramic Capacitor [capacitance=10pF package="100 mil [THT, multilayer]"]
  C5 = Ceramic Capacitor [capacitance=10pF package="100 mil [THT, multilayer]"]

nets:
  N1: U1.connector3, U2.connector3, R2.Pin_1, IC1.pin1, IC1.pin8, C1.0, C2.-, C3.-, TRS1.Sleeve, IC2.pin4, CONN1.chassis6, R3.Pin_0, R4.Pin_0, J1.pin1, C4.0, C5.0
  N2: U1.connector4, U2.connector5, R1.Pin_0, R2.Pin_0
  N3: U1.connector5, U2.connector4, IC2.pin6
  N4: U1.connector6, TRS1.Tip, R3.Pin_1
  N5: U1.connector7, U2.connector7, IC1.pin4, D1.cathode, C1.1, C3.+
  N6: U2.connector6, TRS1.Ring, R4.Pin_1
  N7: R1.Pin_1, IC1.pin2, IC1.pin6, L1.pin_0, C2.+, IC2.pin8, CONN1.5V
  N8: IC1.pin7, L1.pin_1, D1.anode
  N9: IC2.pin2, XTAL1.pin_1, C5.1
  N10: IC2.pin3, XTAL1.pin_0, C4.1
  N11: IC2.pin5, J1.pin2
